// Logisim project projetos.circ as structural Verilog: 3 circuits, main circuit breg
module main (
);

  wire clk, comparator_1_eq, jalr, mux_ula, pcreg, wbreg, wm;
  wire [1:0] dado_breg, pc_sel;
  wire [3:0] opcode, opula;
  wire [7:0] rom_2_data;
  wire [11:0] adder_1_out, adder_2_out, imm, multiplexer_1_out, multiplexer_3_out, multiplexer_4_out, pc_imm,
       pc_q, pc_reg, ra, ram_1_dout, rb, ula_1_resultado;

  Clock clock_1 (.out(clk));
  Multiplexer #(.select(2), .width(12)) multiplexer_1 (
    .in0(adder_2_out), .in1(pc_imm), .in2(pc_reg), .out(multiplexer_1_out), .sel(pc_sel));  // open: in3
  Register #(.width(12)) pc (.D(multiplexer_1_out), .en(1'b1), .clk(clk), .Q(pc_q));  // open: clr
  Adder #(.width(12)) adder_1 (.a(adder_2_out), .b(rb), .out(adder_1_out));  // open: cin, cout
  ROM #(.addrWidth(4), .dataWidth(12)) rom_1 (
    .addr(opcode), .data({pc_sel, wbreg, mux_ula, dado_breg, wm, opula, jalr}));
  Multiplexer #(.width(12)) multiplexer_2 (.in0(adder_2_out), .in1(adder_1_out), .out(pc_reg), .sel(pcreg));
  Adder #(.width(12)) adder_2 (.a(pc_q), .b(12'h1), .out(adder_2_out));  // open: cin, cout
  ROM #(.addrWidth(12), .dataWidth(12)) rom_2 (.addr(pc_q), .data({opcode, rom_2_data}));
  Adder #(.width(12)) adder_3 (.a(pc_q), .b(imm), .out(pc_imm));  // open: cin, cout
  Comparator #(.width(12)) comparator_1 (.a(ra), .b({12{1'b0}}), .eq(comparator_1_eq));  // open: gt, lt
  or or_1 (pcreg, comparator_1_eq, jalr);
  assign imm = {{8{rom_2_data[3]}}, rom_2_data[3:0]};  // Bit_Extender bit_extender_1
  Multiplexer #(.select(2), .width(12)) multiplexer_3 (
    .in0(ula_1_resultado), .in1(ram_1_dout), .in2(pc_imm), .in3(pc_reg), .out(multiplexer_3_out),
    .sel(dado_breg));
  breg breg_1 (
    .D(multiplexer_3_out), .rs1(rom_2_data[7:4]), .rs2(rom_2_data[3:0]), .rd(rom_2_data[7:4]), .w(wbreg),
    .clk(clk), .a(ra), .b(rb));
  Multiplexer #(.width(12)) multiplexer_4 (.in0(rb), .in1(imm), .out(multiplexer_4_out), .sel(mux_ula));
  ula ula_1 (.A(ra), .B(multiplexer_4_out), .opula(opula), .resultado(ula_1_resultado));
  RAM #(.addrWidth(12), .dataWidth(12)) ram_1 (.addr(rb), .we(wm), .oe(1'b1), .clk(clk), .din(ra), .dout(ram_1_dout));

  // Notes on the sheet:
  //   contents of rom_1 (hex, n*v repeats v):
  //   202 204 206 208 20a 20c 20e 210 212 302 240 20 680 a41 8c0 214
  //   contents of rom_2 (hex, n*v repeats v):
  //   8bb 8cc 9c7 9c3 8dd dc dc 899 9c 811 822 29 121 833 39 39 935 e23 844 4b 41 866 a64 a64 855 5c 51
  //   877 a75 a75 822 2d 21 67 b62 911 844 4*948 d04
endmodule

module breg (
  input  [11:0] D,
  input  [3:0] rs1,
  input  [3:0] rs2,
  input  [3:0] rd,
  input  w,
  input  clk,
  output [11:0] a,
  output [11:0] b
);

  wire r1, r2, r3, r4, r5, r6, r7, r8, r9, r10, r11, r12, r13, r14, r15;
  wire [11:0] multiplexer_1_out, multiplexer_2_out, multiplexer_3_out, multiplexer_4_out, multiplexer_5_out,
       multiplexer_6_out, multiplexer_7_out, multiplexer_8_out, multiplexer_9_out, multiplexer_10_out,
       multiplexer_11_out, multiplexer_12_out, multiplexer_13_out, multiplexer_14_out, multiplexer_15_out,
       vr1, vr2, vr3, vr4, vr5, vr6, vr7, vr8, vr9, vr10, vr11, vr12, vr13, vr14, vr15;

  Demultiplexer #(.select(4)) demultiplexer_1 (
    .out1(r1), .out2(r2), .out3(r3), .out4(r4), .out5(r5), .out6(r6), .out7(r7), .out8(r8), .out9(r9),
    .out10(r10), .out11(r11), .out12(r12), .out13(r13), .out14(r14), .out15(r15), .in(w), .sel(rd));  // open: out0
  Multiplexer #(.width(12)) multiplexer_1 (.in0(vr1), .in1(D), .out(multiplexer_1_out), .sel(r1));
  Multiplexer #(.width(12)) multiplexer_2 (.in0(vr2), .in1(D), .out(multiplexer_2_out), .sel(r2));
  Multiplexer #(.width(12)) multiplexer_3 (.in0(vr3), .in1(D), .out(multiplexer_3_out), .sel(r3));
  Multiplexer #(.width(12)) multiplexer_4 (.in0(vr4), .in1(D), .out(multiplexer_4_out), .sel(r4));
  Multiplexer #(.width(12)) multiplexer_5 (.in0(vr5), .in1(D), .out(multiplexer_5_out), .sel(r5));
  Multiplexer #(.width(12)) multiplexer_6 (.in0(vr6), .in1(D), .out(multiplexer_6_out), .sel(r6));
  Multiplexer #(.width(12)) multiplexer_7 (.in0(vr7), .in1(D), .out(multiplexer_7_out), .sel(r7));
  Multiplexer #(.width(12)) multiplexer_8 (.in0(vr8), .in1(D), .out(multiplexer_8_out), .sel(r8));
  Multiplexer #(.width(12)) multiplexer_9 (.in0(vr9), .in1(D), .out(multiplexer_9_out), .sel(r9));
  Multiplexer #(.width(12)) multiplexer_10 (.in0(vr10), .in1(D), .out(multiplexer_10_out), .sel(r10));
  Multiplexer #(.width(12)) multiplexer_11 (.in0(vr11), .in1(D), .out(multiplexer_11_out), .sel(r11));
  Multiplexer #(.width(12)) multiplexer_12 (.in0(vr12), .in1(D), .out(multiplexer_12_out), .sel(r12));
  Multiplexer #(.width(12)) multiplexer_13 (.in0(vr13), .in1(D), .out(multiplexer_13_out), .sel(r13));
  Multiplexer #(.width(12)) multiplexer_14 (.in0(vr14), .in1(D), .out(multiplexer_14_out), .sel(r14));
  Multiplexer #(.width(12)) multiplexer_15 (.in0(vr15), .in1(D), .out(multiplexer_15_out), .sel(r15));
  Register #(.width(12)) u_r1 (.D(multiplexer_1_out), .clk(clk), .Q(vr1));  // open: en, clr
  Register #(.width(12)) u_r2 (.D(multiplexer_2_out), .clk(clk), .Q(vr2));  // open: en, clr
  Register #(.width(12)) u_r3 (.D(multiplexer_3_out), .clk(clk), .Q(vr3));  // open: en, clr
  Register #(.width(12)) u_r4 (.D(multiplexer_4_out), .clk(clk), .Q(vr4));  // open: en, clr
  Register #(.width(12)) u_r5 (.D(multiplexer_5_out), .clk(clk), .Q(vr5));  // open: en, clr
  Register #(.width(12)) u_r6 (.D(multiplexer_6_out), .clk(clk), .Q(vr6));  // open: en, clr
  Register #(.width(12)) u_r7 (.D(multiplexer_7_out), .clk(clk), .Q(vr7));  // open: en, clr
  Register #(.width(12)) u_r8 (.D(multiplexer_8_out), .clk(clk), .Q(vr8));  // open: en, clr
  Register #(.width(12)) u_r9 (.D(multiplexer_9_out), .clk(clk), .Q(vr9));  // open: en, clr
  Register #(.width(12)) u_r10 (.D(multiplexer_10_out), .clk(clk), .Q(vr10));  // open: en, clr
  Register #(.width(12)) u_r11 (.D(multiplexer_11_out), .clk(clk), .Q(vr11));  // open: en, clr
  Register #(.width(12)) u_r12 (.D(multiplexer_12_out), .clk(clk), .Q(vr12));  // open: en, clr
  Register #(.width(12)) u_r13 (.D(multiplexer_13_out), .clk(clk), .Q(vr13));  // open: en, clr
  Register #(.width(12)) u_r14 (.D(multiplexer_14_out), .clk(clk), .Q(vr14));  // open: en, clr
  Register #(.width(12)) u_r15 (.D(multiplexer_15_out), .clk(clk), .Q(vr15));  // open: en, clr
  Multiplexer #(.select(4), .width(12)) multiplexer_16 (
    .in0({12{1'b0}}), .in1(vr1), .in2(vr2), .in3(vr3), .in4(vr4), .in5(vr5), .in6(vr6), .in7(vr7), .in8(vr8),
    .in9(vr9), .in10(vr10), .in11(vr11), .in12(vr12), .in13(vr13), .in14(vr14), .in15(vr15), .out(a),
    .sel(rs1));
  Multiplexer #(.select(4), .width(12)) multiplexer_17 (
    .in0({12{1'b0}}), .in1(vr1), .in2(vr2), .in3(vr3), .in4(vr4), .in5(vr5), .in6(vr6), .in7(vr7), .in8(vr8),
    .in9(vr9), .in10(vr10), .in11(vr11), .in12(vr12), .in13(vr13), .in14(vr14), .in15(vr15), .out(b),
    .sel(rs2));
endmodule

module ula (
  input  [11:0] A,
  input  [11:0] B,
  input  [3:0] opula,
  output [11:0] resultado
);

  wire [11:0] add, div, mul, Sand, slr, Snot, Sor, Ssll, sub, Sxor;

  Adder #(.width(12)) adder_1 (.a(A), .b(B), .out(add));  // open: cin, cout
  Subtractor #(.width(12)) subtractor_1 (.a(A), .b(B), .out(sub));  // open: bin, bout
  Multiplier #(.width(12)) multiplier_1 (.a(A), .b(B), .out(mul));  // open: cin, cout
  Divider #(.width(12)) divider_1 (.a(A), .b(B), .out(div));  // open: upper, rem
  Shifter #(.width(12)) shifter_1 (.in(A), .\dist (B[3:0]), .out(Ssll));
  Shifter #(.shift("lr"), .width(12)) shifter_2 (.in(A), .\dist (B[3:0]), .out(slr));
  assign Sand = A & B;  // AND_Gate and_1, 12 bits wide
  assign Sor = A | B;  // OR_Gate or_1, 12 bits wide
  assign Sxor = A ^ B;  // XOR_Gate xor_1, 12 bits wide
  assign Snot = ~A;  // NOT_Gate not_1, 12 bits wide
  Multiplexer #(.select(4), .width(12)) multiplexer_1 (
    .in1(add), .in2(sub), .in3(mul), .in4(div), .in5(Ssll), .in6(slr), .in7(Sand), .in8(Sor), .in9(Sxor),
    .in10(Snot), .out(resultado), .sel(opula));  // open: in0, in11, in12, in13, in14, in15

  // Other names for the same wires on the sheet: f[3:0] = opula
endmodule
